# Fritzing sketch Aviso Sonoro1 (saved by Fritzing 0.8.7b)
circuit board: 5.26752cm x 4.3902cm
breadboards: 1

parts:
  Q2 = NPN-Transistor [part_number=2N3904 package="TO92 [THT]"]
  LED = LED - 5mm [color="Red (633nm)" package="5 mm [THT]"]
  D1 = Rectifier Diode [part_number=1N914 package="300 mil [THT]"]
  R1 = Resistor [tolerance=±5% resistance=10k package=THT]
  R2 = Resistor [tolerance=±5% resistance=10k package=THT]
  R3 = Resistor [tolerance=±5% resistance=220 package=THT]
  R4 = Resistor [tolerance=±5% resistance=4.7k package=THT]
  R5 = Resistor [tolerance=±5% resistance=3.3k package=THT]
  Falante_Piezo = Piezo Speaker
  Q1 = NPN-Transistor [part_number=2N3904 package="TO92 [THT]"]
  D2 = Rectifier Diode [part_number=1N4001 package="300 mil [THT]"]
  J2 = screw terminal, 4 pins

nets:
  N1: Q2.E, R3.Pin_1
  N2: Q2.B, R1.Pin_0, R4.Pin_1
  N3: Q2.C, LED.cathode, D1.cathode
  N4: LED.anode, Falante_Piezo.pin1, D2.cathode
  N5: D1.anode, R2.Pin_1, Q1.E
  N6: R1.Pin_1, Falante_Piezo.pin2, Q1.C, D2.anode, J2.pin1, J2.pin2
  GND: R2.Pin_0, R3.Pin_0, R4.Pin_0, J2.pin4
  N7: R5.Pin_0, Q1.B
  12V: R5.Pin_1, J2.pin3
